// Digital circuit diglab_07_03.dig as structural Verilog
module diglab_07_03 (
  input  J,
  input  K,
  input  Clear,
  input  Clock,
  output Q,
  output Q_2
);

  wire and_1_out, and_2_out, and_3_out, and_4_out, and_5_out, not_1_out, not_2_out, or_1_out, or_2_out,
       or_3_out, rs_ff_as_1_nq, rs_ff_as_1_q;

  not not_1 (not_1_out, Clock);
  not not_2 (not_2_out, Clear);
  or or_1 (or_1_out, K, Clear);
  and and_1 (and_1_out, J, not_2_out);
  or or_2 (or_2_out, Clock, Clear);
  and and_2 (and_2_out, Q, or_1_out, or_2_out);
  and and_3 (and_3_out, or_2_out, and_1_out, Q_2);
  RS_FF_AS rs_ff_as_1 (.S(and_3_out), .R(and_2_out), .Q(rs_ff_as_1_q), .nQ(rs_ff_as_1_nq));
  or or_3 (or_3_out, not_1_out, Clear);
  and and_4 (and_4_out, or_3_out, rs_ff_as_1_nq);
  and and_5 (and_5_out, rs_ff_as_1_q, or_3_out);
  RS_FF_AS rs_ff_as_2 (.S(and_5_out), .R(and_4_out), .Q(Q), .nQ(Q_2));
endmodule
