// Digital circuit diglab_07_05.dig as structural Verilog
module diglab_07_05 (
  input  T,
  input  Clear,
  input  Clock,
  output Q,
  output Q_2
);

  wire and_1_out, and_2_out, not_1_out, not_2_out, not_3_out, or_1_out, t_ff_1_nq, t_ff_1_q;

  not not_1 (not_1_out, Clear);
  and and_1 (and_1_out, T, not_1_out);
  not not_2 (not_2_out, Clock);
  T_FF t_ff_1 (.T(and_1_out), .C(Clock), .Q(t_ff_1_q), .nQ(t_ff_1_nq));
  and and_2 (and_2_out, t_ff_1_q, not_1_out);
  not not_3 (not_3_out, not_2_out);
  or or_1 (or_1_out, t_ff_1_nq, Clear);
  RS_FF rs_ff_1 (.S(and_2_out), .C(not_3_out), .R(or_1_out), .Q(Q), .nQ(Q_2));
endmodule
