// Digital circuit dig_logic_cp_midterm_2023_02.dig as structural Verilog
module dig_logic_cp_midterm_2023_02 (
  input  [7:0] in0,
  input  [7:0] in1,
  input  addsubtract,
  output [4:0] out
);

  wire add_1_c_o, add_2_c_o, add_3_c_o, add_4_c_o, add_5_c_o, add_6_c_o, add_7_c_o, add_8_c_o, add_9_c_o,
       add_10_c_o, add_11_c_o, add_12_c_o, add_13_c_o, add_14_c_o, add_15_c_o, add_16_c_o;
  wire [3:0] add_1_s, add_2_s, add_3_s, add_4_s, add_5_s, add_6_s, add_7_s, add_8_s, add_9_s, add_10_s,
       add_11_s, add_12_s, add_13_s, add_14_s;
  wire [4:0] add_15_s, add_16_s, not_1_out;

  Add #(.Bits(4)) add_1 (.a({3'b000, in0[0]}), .b({3'b000, in0[1]}), .c_i(1'b0), .s(add_1_s), .c_o(add_1_c_o));
  Add #(.Bits(4)) add_2 (.a(add_1_s), .b({3'b000, in0[2]}), .c_i(add_1_c_o), .s(add_2_s), .c_o(add_2_c_o));
  Add #(.Bits(4)) add_3 (.a(add_2_s), .b({3'b000, in0[3]}), .c_i(add_2_c_o), .s(add_3_s), .c_o(add_3_c_o));
  Add #(.Bits(4)) add_4 (.a(add_3_s), .b({3'b000, in0[4]}), .c_i(add_3_c_o), .s(add_4_s), .c_o(add_4_c_o));
  Add #(.Bits(4)) add_5 (.a(add_4_s), .b({3'b000, in0[5]}), .c_i(add_4_c_o), .s(add_5_s), .c_o(add_5_c_o));
  Add #(.Bits(4)) add_6 (.a(add_5_s), .b({3'b000, in0[6]}), .c_i(add_5_c_o), .s(add_6_s), .c_o(add_6_c_o));
  Add #(.Bits(4)) add_7 (.a(add_6_s), .b({3'b000, in0[7]}), .c_i(add_6_c_o), .s(add_7_s), .c_o(add_7_c_o));
  Add #(.Bits(4)) add_8 (.a({3'b000, in1[0]}), .b({3'b000, in1[1]}), .c_i(1'b0), .s(add_8_s), .c_o(add_8_c_o));
  Add #(.Bits(4)) add_9 (.a(add_8_s), .b({3'b000, in1[2]}), .c_i(add_8_c_o), .s(add_9_s), .c_o(add_9_c_o));
  Add #(.Bits(4)) add_10 (.a(add_9_s), .b({3'b000, in1[3]}), .c_i(add_9_c_o), .s(add_10_s), .c_o(add_10_c_o));
  Add #(.Bits(4)) add_11 (.a(add_10_s), .b({3'b000, in1[4]}), .c_i(add_10_c_o), .s(add_11_s), .c_o(add_11_c_o));
  Add #(.Bits(4)) add_12 (.a(add_11_s), .b({3'b000, in1[5]}), .c_i(add_11_c_o), .s(add_12_s), .c_o(add_12_c_o));
  Add #(.Bits(4)) add_13 (.a(add_12_s), .b({3'b000, in1[6]}), .c_i(add_12_c_o), .s(add_13_s), .c_o(add_13_c_o));
  Add #(.Bits(4)) add_14 (.a(add_13_s), .b({3'b000, in1[7]}), .c_i(add_13_c_o), .s(add_14_s), .c_o(add_14_c_o));
  PullDown pulldown_1 (.out(add_7_c_o));
  PullDown pulldown_2 (.out(add_14_c_o));
  assign not_1_out = ~{1'b0, add_14_s};  // Not not_1, 5 bits wide
  Add #(.Bits(5)) add_15 (.a({1'b0, add_7_s}), .b({1'b0, add_14_s}), .c_i(1'b0), .s(add_15_s), .c_o(add_15_c_o));
  Add #(.Bits(5)) add_16 (.a({1'b0, add_7_s}), .b(not_1_out), .c_i(1'b1), .s(add_16_s), .c_o(add_16_c_o));
  PullDown pulldown_3 (.out(add_15_c_o));
  PullDown pulldown_4 (.out(add_16_c_o));
  Multiplexer #(.Bits(5)) multiplexer_1 (.sel(addsubtract), .in_0(add_15_s), .in_1(add_16_s), .out(out));
endmodule
