// Digital circuit diglab_2023_final_01.dig as structural Verilog
module diglab_2023_final_01 (
  input  reset,
  input  clk,
  output A,
  output B,
  output C
);

  wire [2:0] add_1_s, d_ff_1_q, multiplexer_1_out, rom_1_d;

  Add #(.Bits(3)) add_1 (.a(d_ff_1_q), .b(3'b001), .c_i(1'b0), .s(add_1_s));  // open: c_o
  Multiplexer #(.Bits(3)) multiplexer_1 (.sel(reset), .in_0(add_1_s), .in_1(3'b001), .out(multiplexer_1_out));
  D_FF #(.Bits(3)) d_ff_1 (.D(multiplexer_1_out), .C(clk), .Q(d_ff_1_q));  // open: nQ
  ROM #(.AddrBits(3), .Bits(3)) rom_1 (.A(d_ff_1_q), .sel(1'b1), .D(rom_1_d));
  D_FF #(.Bits(3)) d_ff_2 (.D(rom_1_d), .C(clk), .Q({C, B, A}));  // open: nQ

  // Notes on the sheet:
  //   contents of rom_1 (hex, n*v repeats v):
  //   0,2,4,1,3,6,5,7
endmodule

/* Test case TestCase:
clk reset C B A
0 0 0 0 0 
0 1 0 0 0
1 1 0 0 0
0 0 0 0 0
1 0 0 1 0
0 0 0 1 0
1 0 1 0 0
0 0 1 0 0 
1 0 0 0 1
0 0 0 0 1
1 0 0 1 1
0 0 0 1 1
1 0 1 1 0
0 0 1 1 0
1 0 1 0 1
0 0 1 0 1
1 0 1 1 1
0 0 1 1 1
1 0 0 0 0
0 0 0 0 0
1 0 0 1 0
0 0 0 1 0
1 0 1 0 0
0 0 1 0 0 
1 0 0 0 1
0 0 0 0 1
1 0 0 1 1
0 0 0 1 1
1 0 1 1 0
0 0 1 1 0
1 0 1 0 1
0 0 1 0 1
1 0 1 1 1
0 0 1 1 1
*/
