// Digital circuit diglab_2023_final_02.dig as structural Verilog
module diglab_2023_final_02 (
  input  [15:0] A,
  input  \input ,
  input  clk,
  output [7:0] sqrt,
  output busy
);

  wire and_1_out, comparator_1_eq, comparator_1_lt, comparator_2_lt, comparator_3_gt, multiplexer_8_out,
       or_1_out;
  wire [2:0] multiplexer_1_out, multiplexer_2_out, multiplexer_3_out, multiplexer_4_out, useState_q;
  wire [8:0] add_1_s, div_1_q, max, mid, multiplexer_5_out, multiplexer_6_out, multiplexer_7_out, sub_1_s,
       sub_2_s, sub_3_s;
  wire [8:8] min;
  wire [17:0] mul_1_mul, mul_2_mul, mul_3_mul;

  Add #(.Bits(9)) add_1 (.a({min[8], sqrt}), .b(9'h1), .c_i(1'b0), .s(add_1_s));  // open: c_o
  Mul #(.Bits(9)) mul_1 (.a({min[8], sqrt}), .b({min[8], sqrt}), .mul(mul_1_mul));
  Mul #(.Bits(9)) mul_2 (.a(add_1_s), .b(add_1_s), .mul(mul_2_mul));
  Mul #(.Bits(9)) mul_3 (.a(mid), .b(mid), .mul(mul_3_mul));
  Sub #(.Bits(9)) sub_1 (.a(max), .b({min[8], sqrt}), .c_i(1'b0), .s(sub_1_s));  // open: c_o
  Div #(.Bits(9)) div_1 (.a(sub_1_s), .b(9'h2), .q(div_1_q));  // open: r
  Comparator #(.Bits(18)) comparator_1 (
    .a(mul_1_mul), .b({2'b00, A}), .eq(comparator_1_eq), .lt(comparator_1_lt));  // open: gt
  Comparator #(.Bits(18)) comparator_2 (.a({2'b00, A}), .b(mul_2_mul), .lt(comparator_2_lt));  // open: gt, eq
  Comparator #(.Bits(18)) comparator_3 (.a(mul_3_mul), .b({2'b00, A}), .gt(comparator_3_gt));  // open: eq, lt
  or or_1 (or_1_out, comparator_1_eq, comparator_1_lt);
  Multiplexer #(.Bits(3)) multiplexer_1 (.sel(\input ), .in_0(3'b000), .in_1(3'b001), .out(multiplexer_1_out));
  Multiplexer #(.Bits(3)) multiplexer_2 (.sel(and_1_out), .in_0(3'b011), .in_1(3'b110), .out(multiplexer_2_out));
  Multiplexer #(.Bits(3)) multiplexer_3 (.sel(comparator_3_gt), .in_0(3'b101), .in_1(3'b100), .out(multiplexer_3_out));
  Sub #(.Bits(9)) sub_2 (.a(mid), .b(9'h1), .c_i(1'b0), .s(sub_2_s));  // open: c_o
  Sub #(.Bits(9)) sub_3 (.a(max), .b(div_1_q), .c_i(1'b0), .s(sub_3_s));  // open: c_o
  and and_1 (and_1_out, or_1_out, comparator_2_lt);
  Multiplexer #(.Bits(3), .Selector_Bits(3)) multiplexer_4 (
    .sel(useState_q), .in_0(multiplexer_1_out), .in_1(3'b010), .in_2(multiplexer_2_out),
    .in_3(multiplexer_3_out), .in_4(3'b010), .in_5(3'b010), .in_6(3'b110), .in_7(3'b000),
    .out(multiplexer_4_out));
  Multiplexer #(.Selector_Bits(3), .Bits(9)) multiplexer_5 (
    .sel(useState_q), .in_0({min[8], sqrt}), .in_1({9{1'b0}}), .in_2({min[8], sqrt}), .in_3({min[8], sqrt}),
    .in_4({min[8], sqrt}), .in_5(mid), .in_6({min[8], sqrt}), .in_7({9{1'b0}}), .out(multiplexer_5_out));
  Multiplexer #(.Selector_Bits(3), .Bits(9)) multiplexer_6 (
    .sel(useState_q), .in_0(max), .in_1(9'hff), .in_2(max), .in_3(max), .in_4(sub_2_s), .in_5(max),
    .in_6(max), .in_7({9{1'b0}}), .out(multiplexer_6_out));
  Multiplexer #(.Selector_Bits(3), .Bits(9)) multiplexer_7 (
    .sel(useState_q), .in_0(mid), .in_1(mid), .in_2(sub_3_s), .in_3(mid), .in_4(mid), .in_5(mid), .in_6(mid),
    .in_7({9{1'b0}}), .out(multiplexer_7_out));
  D_FF #(.Bits(3)) useState (.D(multiplexer_4_out), .C(clk), .Q(useState_q));  // open: nQ
  D_FF #(.Bits(9)) u_min (.D(multiplexer_5_out), .C(clk), .Q({min[8], sqrt}));  // open: nQ
  D_FF #(.Bits(9)) u_max (.D(multiplexer_6_out), .C(clk), .Q(max));  // open: nQ
  D_FF #(.Bits(9)) u_mid (.D(multiplexer_7_out), .C(clk), .Q(mid));  // open: nQ
  Multiplexer #(.Selector_Bits(3)) multiplexer_8 (
    .sel(useState_q), .in_0(busy), .in_1(1'b1), .in_2(busy), .in_3(busy), .in_4(busy), .in_5(busy),
    .in_6(1'b0), .in_7(1'b0), .out(multiplexer_8_out));
  D_FF u_busy (.D(multiplexer_8_out), .C(clk), .Q(busy));  // open: nQ
  PullDown pulldown_1 (.out(min[8]));

  // Other names for the same wires on the sheet: min[7:0] = sqrt

  // Notes on the sheet:
  //   clk: Hz: 10
endmodule

/* Test case TestCase1:
clk A input sqrt busy
0 0 0 0 0
1 0 0 0 0
0 0 0 0 0
1 0 0 0 0
0 0 1 X X
1 0 1 X X
repeat (80) C 0 0 X X
0 0 0 0 0
1 0 0 0 0
*/

/* Test case TestCase2:
clk A input sqrt busy
0 0 0 0 0
1 0 0 0 0
0 0 0 0 0
1 0 0 0 0
0 1 1 X X
1 1 1 X X
repeat (80) C 1 0 X X
0 0 0 1 0
1 0 0 1 0
*/

/* Test case TestCase3:
clk A input sqrt busy
0 0 0 0 0
1 0 0 0 0
0 0 0 0 0
1 0 0 0 0
0 4 1 X X
1 4 1 X X
repeat (80) C 4 0 X X
0 0 0 2 0
1 0 0 2 0
*/

/* Test case TestCase4:
clk A input sqrt busy
0 0 0 0 0
1 0 0 0 0
0 0 0 0 0
1 0 0 0 0
0 9 1 X X
1 9 1 X X
repeat (80) C 9 0 X X
0 0 0 3 0
1 0 0 3 0
*/

/* Test case TestCase5:
clk A input sqrt busy
0 0 0 0 0
1 0 0 0 0
0 0 0 0 0
1 0 0 0 0
0 8 1 X X
1 8 1 X X
repeat (80) C 8 0 X X
0 0 0 2 0
1 0 0 2 0
*/

/* Test case TestCase Custom1:
clk A input sqrt busy
0 0 0 0 0
1 0 0 0 0
0 0 0 0 0
1 0 0 0 0
0 1 1 X X
1 1 1 X X
repeat (80) C 1 0 X X
0 0 0 1 0
1 0 0 1 0
*/

/* Test case TestCase Custom2:
clk A input sqrt busy
0 0 0 0 0
1 0 0 0 0
0 0 0 0 0
1 0 0 0 0
0 0 1 X X
1 0 1 X X
repeat (80) C 0 0 X X
0 0 0 0 0
1 0 0 0 0
*/

/* Test case TestCase Custom3:
clk A input sqrt busy
0 0 0 0 0
1 0 0 0 0
0 0 0 0 0
1 0 0 0 0
0 65535 1 X X
1 65535 1 X X
repeat (80) C 65535 0 X X
0 0 0 255 0
1 0 0 255 0
*/
