// Digital circuit diglab_2023_final_03.dig as structural Verilog
module diglab_2023_final_03 (
  input  [15:0] A,
  input  \input ,
  input  clk,
  input  reset,
  output [15:0] second
);

  wire and_1_out, comparator_1_gt, comparator_2_gt, not_1_out, or_1_out;
  wire [15:0] first__eq__A__gt__first___A___first_q, multiplexer_1_out, multiplexer_2_out, multiplexer_3_out,
       multiplexer_4_out, multiplexer_5_out;

  or or_1 (or_1_out, clk, reset);
  and and_1 (and_1_out, or_1_out, \input );
  Comparator #(.Bits(16)) comparator_1 (.a(A), .b(second), .gt(comparator_1_gt));  // open: eq, lt
  Comparator #(.Bits(16)) comparator_2 (
    .a(A), .b(first__eq__A__gt__first___A___first_q), .gt(comparator_2_gt));  // open: eq, lt
  Multiplexer #(.Bits(16)) multiplexer_1 (.sel(comparator_1_gt), .in_0(second), .in_1(A), .out(multiplexer_1_out));
  Multiplexer #(.Bits(16)) multiplexer_2 (
    .sel(comparator_2_gt), .in_0(first__eq__A__gt__first___A___first_q), .in_1(A), .out(multiplexer_2_out));
  not not_1 (not_1_out, comparator_2_gt);
  Multiplexer #(.Bits(16)) multiplexer_3 (
    .sel(not_1_out), .in_0(first__eq__A__gt__first___A___first_q), .in_1(multiplexer_1_out),
    .out(multiplexer_3_out));
  Multiplexer #(.Bits(16)) multiplexer_4 (
    .sel(reset), .in_0(multiplexer_2_out), .in_1({16{1'b0}}), .out(multiplexer_4_out));
  Multiplexer #(.Bits(16)) multiplexer_5 (
    .sel(reset), .in_0(multiplexer_3_out), .in_1({16{1'b0}}), .out(multiplexer_5_out));
  D_FF #(.Bits(16)) first__eq__A__gt__first___A___first (
    .D(multiplexer_4_out), .C(and_1_out), .Q(first__eq__A__gt__first___A___first_q));  // open: nQ
  D_FF #(.Bits(16)) second__eq__A__lt__eq__first___A__gt__second___A___second___first (
    .D(multiplexer_5_out), .C(and_1_out), .Q(second));  // open: nQ

  // Notes on the sheet:
  //   clk: Hz: 200
endmodule

/* Test case Case1:
clk A input reset second
0 0 0 0 0
1 0 0 0 0
0 0 0 1 0
1 0 0 1 0
0 0  0 0 0
1 0  0 0 0
0 5 1 0 X
1 5 1 0 X
0  0 0 0 0
1  0 0 0 0
0 12 1 0 X
1 12 1 0 X
0  0 0 0 X
1  0 0 0 5
*/

/* Test case Case2:
clk A input reset second
0 0 0 0 0
1 0 0 0 0
0 0 0 1 0
1 0 0 1 0
0 0  0 0 0
1 0  0 0 0
0 5 1 0 X
1 5 1 0 X
0  0 0 0 0
1  0 0 0 0
0 15 1 0 X
1 15 1 0 X
0  0 0 0 X
1  0 0 0 5
*/

/* Test case Case3:
clk A input reset second
0 0 0 0 0
1 0 0 0 0
0 0 0 1 0
1 0 0 1 0
0 0  0 0 0
1 0  0 0 0
0 65535 1 0 X
1 65535 1 0 X
0  0 0 0 0
1  0 0 0 0
0 65524 1 0 X
1 65524 1 0 X
0  0 0 0 X
1  0 0 0 65524
*/
